# Fritzing sketch diagram (saved by Fritzing 0.9.3b)

parts:
  HC-SR04_Sensor_1 = HC-SR04 Ultrasonic Distance Sensor
  Raspberry_Pi1 = Raspberry Pi B rev2
  R1 = Resistor [tolerance=±5% resistance=500 package=THT]
  R2 = Resistor [tolerance=±5% resistance=220 package=THT]
  R3 = Resistor [tolerance=±5% resistance=220 package="1206 [SMD]"]
  LED1 = smd LED [color="Red (633nm)" package="1206 [SMD]"]

nets:
  VCC: HC-SR04_Sensor_1.VCC, Raspberry_Pi1.5V
  N1: HC-SR04_Sensor_1.TRIG, Raspberry_Pi1.GPIO_18
  N2: HC-SR04_Sensor_1.ECHO, R1.Pin_0, R2.Pin_1
  GND: HC-SR04_Sensor_1.GND, Raspberry_Pi1.GND, R1.Pin_1, R3.Pin_1
  N3: Raspberry_Pi1.GPIO_23, LED1.cathode
  N4: Raspberry_Pi1.GPIO_24, R2.Pin_0
